// Logisim project logisim final build (2 displays).circ as structural Verilog: 1 circuit, main circuit main
module main (
);

  wire and_1_out, and_2_out, and_3_out, and_4_out, and_5_out, and_6_out, and_7_out, and_8_out, and_9_out,
       and_10_out, and_11_out, and_12_out, and_13_out, and_14_out, and_15_out, and_16_out, and_17_out,
       and_18_out, and_19_out, and_20_out, and_21_out, and_22_out, and_23_out, and_24_out, and_25_out,
       and_26_out, and_27_out, and_28_out, and_29_out, and_30_out, and_31_out, and_32_out, and_33_out,
       and_34_out, and_35_out, and_36_out, and_37_out, and_38_out, and_39_out, and_40_out, and_41_out,
       and_42_out, and_43_out, and_44_out, and_45_out, and_46_out, and_47_out, and_48_out, and_49_out,
       and_50_out, and_51_out, and_52_out, and_53_out, and_54_out, clock_1_out, or_1_out, or_2_out, or_3_out,
       or_4_out, or_5_out, or_6_out, or_7_out, or_8_out, or_9_out, or_10_out, or_11_out, or_12_out,
       or_13_out, or_14_out;
  wire [3:0] adder_1_out, counter_1_q, multiplexer_1_out, multiplexer_2_out, register_1_q, register_2_q;
  wire [7:0] rom_1_data;

  Counter #(.width(4), .max('h7), .trigger("falling")) counter_1 (
    .Q(counter_1_q), .clk(clock_1_out));  // open: load, D, count, carry, clr
  Clock clock_1 (.out(clock_1_out));
  ROM #(.addrWidth(4)) rom_1 (.addr(counter_1_q), .data(rom_1_data));  // open: sel
  and and_1 (and_1_out, rom_1_data[5], clock_1_out);
  and and_2 (and_2_out, rom_1_data[4], clock_1_out);
  LED led_1 (.in(register_1_q[1]));
  LED led_2 (.in(register_1_q[3]));
  LED led_3 (.in(register_1_q[2]));
  Register #(.width(4)) register_1 (.D(adder_1_out), .Q(register_1_q), .clk(and_1_out));  // open: en, clr
  Register #(.width(4)) register_2 (.D(adder_1_out), .Q(register_2_q), .clk(and_2_out));  // open: en, clr
  LED led_4 (.in(register_1_q[0]));
  LED led_5 (.in(register_2_q[3]));
  LED led_6 (.in(register_2_q[2]));
  LED led_7 (.in(register_2_q[1]));
  LED led_8 (.in(register_2_q[0]));
  Multiplexer #(.width(4)) multiplexer_1 (
    .in0(rom_1_data[3:0]), .in1(register_1_q), .out(multiplexer_1_out), .sel(rom_1_data[6]));  // open: en
  Multiplexer #(.width(4)) multiplexer_2 (
    .in0(4'b0000), .in1(register_2_q), .out(multiplexer_2_out), .sel(rom_1_data[7]));  // open: en
  Adder #(.width(4)) adder_1 (.a(multiplexer_1_out), .b(multiplexer_2_out), .out(adder_1_out));  // open: cin, cout
  _7_Segment_Display u_7_segment_display_1 (.g(register_1_q[3]));  // open: f, a, b, e, d, c, dp
  _7_Segment_Display u_7_segment_display_2 (
    .g(or_7_out), .f(or_6_out), .a(or_1_out), .b(or_2_out), .e(or_5_out), .d(or_4_out), .c(or_3_out));  // open: dp
  and and_3 (and_3_out, register_1_q[3], ~register_1_q[2]);  // AND_Gate
  and and_4 (and_4_out, register_1_q[1], ~register_1_q[1]);  // AND_Gate
  and and_5 (and_5_out, ~register_1_q[3], register_1_q[1]);  // AND_Gate
  and and_6 (and_6_out, ~register_1_q[2], ~register_1_q[0]);  // AND_Gate
  and and_7 (and_7_out, register_1_q[2], ~register_1_q[1], register_1_q[0]);  // AND_Gate
  and and_8 (and_8_out, ~register_1_q[3], ~register_1_q[2]);  // AND_Gate
  and and_9 (and_9_out, register_1_q[3], register_1_q[2]);
  and and_10 (and_10_out, ~register_1_q[1], ~register_1_q[0]);  // AND_Gate
  and and_11 (and_11_out, register_1_q[3], ~register_1_q[1]);  // AND_Gate
  and and_12 (and_12_out, ~register_1_q[3], register_1_q[1], register_1_q[0]);  // AND_Gate
  and and_13 (and_13_out, ~register_1_q[3], register_1_q[2]);  // AND_Gate
  and and_14 (and_14_out, register_1_q[3], ~register_1_q[2]);  // AND_Gate
  and and_15 (and_15_out, register_1_q[1], ~register_1_q[0]);  // AND_Gate
  and and_16 (and_16_out, ~register_1_q[2], register_1_q[1]);  // AND_Gate
  and and_17 (and_17_out, ~register_1_q[2], ~register_1_q[0]);  // AND_Gate
  and and_18 (and_18_out, register_1_q[2], ~register_1_q[1], register_1_q[0]);  // AND_Gate
  and and_19 (and_19_out, register_1_q[1], ~register_1_q[0]);  // AND_Gate
  and and_20 (and_20_out, ~register_1_q[2], ~register_1_q[0]);  // AND_Gate
  and and_21 (and_21_out, ~register_1_q[1], ~register_1_q[0]);  // AND_Gate
  and and_22 (and_22_out, register_1_q[3], ~register_1_q[2], register_1_q[1]);  // AND_Gate
  and and_23 (and_23_out, ~register_1_q[3], register_1_q[2], ~register_1_q[1]);  // AND_Gate
  and and_24 (and_24_out, ~register_1_q[3], register_1_q[2], ~register_1_q[0]);  // AND_Gate
  and and_25 (and_25_out, register_1_q[1], ~register_1_q[0]);  // AND_Gate
  and and_26 (and_26_out, register_1_q[2], ~register_1_q[1]);  // AND_Gate
  and and_27 (and_27_out, register_1_q[3], ~register_1_q[0]);  // AND_Gate
  and and_28 (and_28_out, ~register_1_q[2], register_1_q[1]);  // AND_Gate
  _7_Segment_Display u_7_segment_display_3 (.g(register_2_q[3]));  // open: f, a, b, e, d, c, dp
  or or_1 (or_1_out, and_3_out, and_4_out, and_5_out, and_6_out, and_7_out);
  or or_2 (or_2_out, and_8_out, and_9_out, and_10_out, and_11_out, and_12_out);
  or or_3 (or_3_out, ~register_1_q[1], register_1_q[0], and_13_out, and_14_out);  // OR_Gate
  or or_4 (or_4_out, and_15_out, and_16_out, and_17_out, and_18_out);
  or or_5 (or_5_out, and_19_out, and_20_out);
  or or_6 (or_6_out, and_21_out, and_22_out, and_23_out, and_24_out);
  or or_7 (or_7_out, and_25_out, and_26_out, and_27_out, and_28_out);
  _7_Segment_Display u_7_segment_display_4 (
    .g(or_14_out), .f(or_13_out), .a(or_8_out), .b(or_9_out), .e(or_12_out), .d(or_11_out), .c(or_10_out));  // open: dp
  and and_29 (and_29_out, register_2_q[3], ~register_2_q[2]);  // AND_Gate
  and and_30 (and_30_out, register_2_q[1], ~register_2_q[1]);  // AND_Gate
  and and_31 (and_31_out, ~register_2_q[3], register_2_q[1]);  // AND_Gate
  and and_32 (and_32_out, ~register_2_q[2], ~register_2_q[0]);  // AND_Gate
  and and_33 (and_33_out, register_2_q[2], ~register_2_q[1], register_2_q[0]);  // AND_Gate
  and and_34 (and_34_out, ~register_2_q[3], ~register_2_q[2]);  // AND_Gate
  and and_35 (and_35_out, register_2_q[3], register_2_q[2]);
  and and_36 (and_36_out, ~register_2_q[1], ~register_2_q[0]);  // AND_Gate
  and and_37 (and_37_out, register_2_q[3], ~register_2_q[1]);  // AND_Gate
  and and_38 (and_38_out, ~register_2_q[3], register_2_q[1], register_2_q[0]);  // AND_Gate
  and and_39 (and_39_out, ~register_2_q[3], register_2_q[2]);  // AND_Gate
  and and_40 (and_40_out, register_2_q[3], ~register_2_q[2]);  // AND_Gate
  and and_41 (and_41_out, register_2_q[1], ~register_2_q[0]);  // AND_Gate
  and and_42 (and_42_out, ~register_2_q[2], register_2_q[1]);  // AND_Gate
  and and_43 (and_43_out, ~register_2_q[2], ~register_2_q[0]);  // AND_Gate
  and and_44 (and_44_out, register_2_q[2], ~register_2_q[1], register_2_q[0]);  // AND_Gate
  and and_45 (and_45_out, register_2_q[1], ~register_2_q[0]);  // AND_Gate
  and and_46 (and_46_out, ~register_2_q[2], ~register_2_q[0]);  // AND_Gate
  and and_47 (and_47_out, ~register_2_q[1], ~register_2_q[0]);  // AND_Gate
  and and_48 (and_48_out, register_2_q[3], ~register_2_q[2], register_2_q[1]);  // AND_Gate
  and and_49 (and_49_out, ~register_2_q[3], register_2_q[2], ~register_2_q[1]);  // AND_Gate
  and and_50 (and_50_out, ~register_2_q[3], register_2_q[2], ~register_2_q[0]);  // AND_Gate
  and and_51 (and_51_out, register_2_q[1], ~register_2_q[0]);  // AND_Gate
  and and_52 (and_52_out, register_2_q[2], ~register_2_q[1]);  // AND_Gate
  and and_53 (and_53_out, register_2_q[3], ~register_2_q[0]);  // AND_Gate
  and and_54 (and_54_out, ~register_2_q[2], register_2_q[1]);  // AND_Gate
  or or_8 (or_8_out, and_29_out, and_30_out, and_31_out, and_32_out, and_33_out);
  or or_9 (or_9_out, and_34_out, and_35_out, and_36_out, and_37_out, and_38_out);
  or or_10 (or_10_out, ~register_2_q[1], register_2_q[0], and_39_out, and_40_out);  // OR_Gate
  or or_11 (or_11_out, and_41_out, and_42_out, and_43_out, and_44_out);
  or or_12 (or_12_out, and_45_out, and_46_out);
  or or_13 (or_13_out, and_47_out, and_48_out, and_49_out, and_50_out);
  or or_14 (or_14_out, and_51_out, and_52_out, and_53_out, and_54_out);

  // Notes on the sheet:
  //   (2*3) - 3 + 2
  //   contents of rom_1 (hex, n*v repeats v):
  //   22 12 d0 d0 2d d0 22 d0
endmodule
